// Logisim project mapa.circ as structural Verilog: 1 circuit, main circuit main
module main (
  input  B0,
  input  B1,
  input  B2,
  input  B3
);

  wire a_out, B1B0_out, B1nB0_out, B2B0_out, B2B1_out, B3B1B0_out, B3B2_out, B3B2B0_out, B3nB0_out,
       B3nB1B0_out, B3nB2_out, B3nB2B0_out, B3nB2B1_out, B3nB2nB0_out, b_out, c_out, d_out, e_out, f_out,
       g_out, nB1B0_out, nB1nB0_out, nB2B0_out, nB2B1_out, nB2nB0_out, nB3B2_out, nB3B2B1_out, nB3nB0_out,
       nB3nB1_out, not_1_out, not_2_out, not_3_out, not_4_out;

  not not_1 (not_1_out, B0);
  not not_2 (not_2_out, B1);
  not not_3 (not_3_out, B2);
  not not_4 (not_4_out, B3);
  and B1B0 (B1B0_out, B1, B0);
  and B2B0 (B2B0_out, B2, B0);
  or g (g_out, B1B0_out, B2B0_out);
  and nB2B1 (nB2B1_out, not_3_out, B1);
  or f (f_out, nB3nB1_out, nB1nB0_out, B3B2B0_out, B3nB2B1_out);
  and B3nB2 (B3nB2_out, B3, not_3_out);
  or e (e_out, nB1nB0_out, nB3nB1_out, B3B2B0_out, B3nB2nB0_out);
  _7_Segment_Display u_7_segment_display_1 (
    .g(g_out), .f(f_out), .a(a_out), .b(b_out), .e(e_out), .d(d_out), .c(c_out));  // open: dp
  and B1nB0 (B1nB0_out, B1, not_1_out);
  or d (d_out, B3nB2_out, B1nB0_out, B3nB0_out, nB2nB0_out, nB3B2B1_out);
  and B3nB0 (B3nB0_out, B3, not_1_out);
  or c (c_out, nB3nB1_out, nB1nB0_out, B3B2_out, nB3nB0_out);
  and B2B1 (B2B1_out, B2, B1);
  or b (b_out, nB1nB0_out, B3B2_out, nB3nB1_out, nB3nB0_out, B3B1B0_out);
  and B3B2 (B3B2_out, B2, B3);
  or a (a_out, B1nB0_out, nB3B2_out, nB3nB0_out, B3nB1B0_out, B3nB2B0_out);
  and nB3B2 (nB3B2_out, not_4_out, B2);
  and nB1B0 (nB1B0_out, not_2_out, B0);
  nor nB3nB0 (nB3nB0_out, B0, B3);
  nor nB2nB0 (nB2nB0_out, B0, B2);
  nor nB1nB0 (nB1nB0_out, B0, B1);
  nor nB3nB1 (nB3nB1_out, B1, B3);
  and nB2B0 (nB2B0_out, not_3_out, B0);
  and B3B2B0 (B3B2B0_out, B2B0_out, B3);
  and B3nB2B1 (B3nB2B1_out, nB2B1_out, B3);
  and B3nB2nB0 (B3nB2nB0_out, nB2nB0_out, B3);
  and nB3B2B1 (nB3B2B1_out, B2B1_out, not_4_out);
  and B3B1B0 (B3B1B0_out, B1B0_out, B3);
  and B3nB1B0 (B3nB1B0_out, nB1B0_out, B3);
  and B3nB2B0 (B3nB2B0_out, nB2B0_out, B3);
endmodule
