// Logisim project secuencia.circ as structural Verilog: 3 circuits, main circuit main
module main (
);

  wire clock_1_out;
  wire [3:0] entrada_1_out_2;
  wire [6:0] salida_1_out_2;

  Clock clock_1 (.out(clock_1_out));
  entrada entrada_1 (.in_1(clock_1_out), .out_2(entrada_1_out_2));
  salida salida_1 (.in_1(entrada_1_out_2), .out_2(salida_1_out_2));
  _7_Segment_Display u_7_segment_display_1 (
    .g(salida_1_out_2[0]), .f(salida_1_out_2[1]), .a(salida_1_out_2[6]), .b(salida_1_out_2[5]),
    .e(salida_1_out_2[2]), .d(salida_1_out_2[3]), .c(salida_1_out_2[4]), .dp(1'b0));
endmodule

module entrada (
  input  in_1,
  output [3:0] out_2
);

  wire B1nB0_out, B3nB0_out, B3nB1_out, B3nB2_out, d_ff_1_q, d_ff_2_q, d_ff_2_qn, d_ff_3_q, d_ff_3_qn,
       d_ff_4_q, d_ff_4_qn, nB0B2_out, nB1B0_out, nB1B2_out, nB2B1B0_out, nB3B2B1B0_out;

  D_Flip_Flop d_ff_1 (.D(out_2[0]), .clk(in_1), .Q(d_ff_1_q), .Qn(out_2[0]));  // open: preset, reset
  D_Flip_Flop d_ff_2 (.D(out_2[1]), .clk(in_1), .Q(d_ff_2_q), .Qn(d_ff_2_qn));  // open: preset, reset
  D_Flip_Flop d_ff_3 (.D(out_2[2]), .clk(in_1), .Q(d_ff_3_q), .Qn(d_ff_3_qn));  // open: preset, reset
  D_Flip_Flop d_ff_4 (.D(in_1), .clk(in_1), .Q(d_ff_4_q), .Qn(d_ff_4_qn));  // open: preset, reset
  and nB1B0 (nB1B0_out, d_ff_2_qn, d_ff_1_q);
  and B1nB0 (B1nB0_out, d_ff_2_q, out_2[0]);
  or B1 (out_2[1], nB1B0_out, B1nB0_out);
  and nB1B2 (nB1B2_out, d_ff_3_q, d_ff_2_qn);
  and nB0B2 (nB0B2_out, d_ff_3_q, out_2[0]);
  or B2 (out_2[2], nB1B2_out, nB0B2_out, nB2B1B0_out);
  and nB2B1B0 (nB2B1B0_out, d_ff_3_qn, d_ff_2_q, d_ff_1_q);
  and B3nB2 (B3nB2_out, d_ff_4_q, d_ff_3_qn);
  and B3nB1 (B3nB1_out, d_ff_4_q, d_ff_2_qn);
  and B3nB0 (B3nB0_out, d_ff_4_q, out_2[0]);
  or B3 (in_1, B3nB2_out, B3nB1_out, B3nB0_out, nB3B2B1B0_out);
  and nB3B2B1B0 (nB3B2B1B0_out, d_ff_4_qn, d_ff_3_q, d_ff_2_q, d_ff_1_q);

  assign out_2[3] = in_1;
endmodule

module salida (
  input  [3:0] in_1,
  output [6:0] out_2
);

  wire B1B0_out, B1nB0_out, B2B0_out, B2B1B0_out, B2nB0_out, B2nB1_out, B2nB1B0_out, B2nB1nB0_out,
       B3B1B0_out, B3B1nB0_out, B3B2_out, B3B2B1_out, B3B2nB0_out, B3nB1_out, B3nB2_out, nB2B1B0_out,
       nB2B1nB0_out, nB3B0_out, nB3B1_out, nB3B2_out, nB3B2B0_out, nB3B2B1nB0_out, nB3nB0_out, nB3nB1B0_out,
       nB3nB2_out, nB3nB2B1_out, not_1_out, not_2_out, not_3_out, not_4_out;

  not not_1 (not_1_out, in_1[0]);
  not not_2 (not_2_out, in_1[1]);
  not not_3 (not_3_out, in_1[2]);
  not not_4 (not_4_out, in_1[3]);
  and nB2B1nB0 (nB2B1nB0_out, B1nB0_out, not_3_out);
  and nB3nB2 (nB3nB2_out, not_4_out, not_3_out);
  and B3nB2 (B3nB2_out, in_1[3], not_3_out);
  and B2nB1B0 (B2nB1B0_out, not_2_out, B2B0_out);
  and nB3B2 (nB3B2_out, not_4_out, in_1[2]);
  and nB3B2B1nB0 (nB3B2B1nB0_out, in_1[1], not_1_out, nB3B2_out);
  and B2B0 (B2B0_out, in_1[2], in_1[0]);
  and nB3nB0 (nB3nB0_out, not_4_out, not_1_out);
  and nB2B1B0 (nB2B1B0_out, not_3_out, B1B0_out);
  and B3nB1 (B3nB1_out, in_1[3], not_2_out);
  and nB3B0 (nB3B0_out, not_4_out, in_1[0]);
  and B2nB1nB0 (B2nB1nB0_out, not_2_out, B2nB0_out);
  and B2nB1 (B2nB1_out, in_1[2], not_2_out);
  and nB3nB1B0 (nB3nB1B0_out, not_2_out, nB3B0_out);
  and nB3B1 (nB3B1_out, not_4_out, in_1[1]);
  and B3B1B0 (B3B1B0_out, in_1[3], B1B0_out);
  and B1B0 (B1B0_out, in_1[1], in_1[0]);
  and B3B2B1 (B3B2B1_out, B3B2_out, in_1[1]);
  and B2nB0 (B2nB0_out, in_1[2], not_1_out);
  and B2B1B0 (B2B1B0_out, in_1[2], B1B0_out);
  and B3B2 (B3B2_out, in_1[3], in_1[2]);
  and nB3nB2B1 (nB3nB2B1_out, nB3nB2_out, in_1[1]);
  and B1nB0 (B1nB0_out, in_1[1], not_1_out);
  and nB3B2B0 (nB3B2B0_out, nB3B2_out, in_1[0]);
  and B3B1nB0 (B3B1nB0_out, in_1[3], B1nB0_out);
  and B3B2nB0 (B3B2nB0_out, B3B2_out, not_1_out);
  or a (out_2[6], B3B2nB0_out, B3B1nB0_out, nB3B2B0_out, nB3nB2B1_out);
  or b (out_2[5], B1B0_out, B2nB1nB0_out, B3B2B1_out);
  or c (out_2[4], B2B1B0_out, B3B2B1_out, B3B1B0_out, nB3nB1B0_out, B2nB1nB0_out);
  or d (out_2[3], nB2B1B0_out, nB3B2B1nB0_out, B2nB1B0_out, B3nB2_out);
  or e (out_2[2], nB3B1_out, B1B0_out, B3nB1_out, not_3_out);
  or f (out_2[1], B2nB1_out, nB3nB0_out, B2B0_out, B3nB2_out);
  or g (out_2[0], nB3B0_out, B2B1B0_out, B2nB1nB0_out, nB2B1nB0_out);
endmodule
